# Fritzing sketch WemosD1_DHT22-BMP180-MQ135 (saved by Fritzing 0.9.3b)
circuit board: 8.46667cm x 5.64444cm
breadboards: 1

parts:
  DHT1 = DHT22 Humidity and Temperature Sensor
  R1 = Resistor [tolerance=±5% resistance=10k package="2512 [SMD]"]
  Componente1 = Barometric Pressure Sensor - BMP180 Breakout (GY-68)
  WeMos_D1_Mini1 = WeMos D1 Mini  # not connected
  Grove1 = Grove OLED 128x96
  U1 = GAS_SENSOR [package=mq-3]

nets (from the breadboard view):
  VCC: DHT1.VDD, Componente1.VCC, Grove1.VCC, U1.H2
  N1: DHT1.DATA, R1.Pin_1
  GND: DHT1.GND, Componente1.GND, Grove1.GND, U1.H1
  N2: Componente1.SCL, Grove1.SCL
  N3: Componente1.SDA, Grove1.SDA
